# Fritzing sketch CanSat Fritzing Sketch (saved by Fritzing 0.9.10b)
breadboards: 1

parts:
  元件1 = Arduino Uno (Rev3)
  BMP280_Breakout1 = BMP280 Breakout Board [part_number=BMP280]
  元件2 = InvenSense MPU6050
  元件3 = SI1145 Digital UV Index + IR + Visible Light Sensor [part_number=1777]
  M1 = NEO-M8N GPS Module [part_number=GY-GPSV3-NEO]
  元件4 = APC220 with antenna

nets:
  N1: 元件1.D8, M1.Rx
  N2: 元件1.D9_PWM, M1.Tx
  N3: 元件1.A4/SDA, BMP280_Breakout1.SDA, 元件2.SDA, 元件3.SDA
  N4: 元件1.A5/SCL, BMP280_Breakout1.SCL, 元件2.SCL, 元件3.SCL
  N5: 元件1.D0/RX, 元件4.TXD
  N6: 元件1.D1/TX, 元件4.RXD
  VCC: 元件1.3V3, BMP280_Breakout1.VCC, 元件2.VCC, 元件3.+3V3, M1.Vcc, 元件4.VCC
  GND: 元件1.GND, BMP280_Breakout1.GND, 元件2.GND, 元件3.GND, M1.GND, 元件4.GND

notes:
  BMP280
  Red: 3v3
  Blue: GND
  Green: SCL
  Yellow: SDA
  Cyan: RXD/TXD
  GPS: AltSoftwareSerial
  Radio: HardwareSerial

custom parts:
  BMP280 Breakout Board: This is a breakout board for the Bosch Sensortec BMP280, "an absolute barometric pressure sensor especially designed for mobile applications." The operation range is 300 to 1100 hPa. Supply voltage is 1.2 to 3.6V. Operating temperature range is -40 to +85 °C.
  SI1145 Digital UV Index + IR + Visible Light Sensor: The SI1145 is a new sensor from SiLabs with a calibrated light sensing algorithm that can calculate UV Index. It doesn't contain an actual UV sensing element, instead it approximates it based on visible & IR light from the sun. We took this outside a couple days and compared the calculated UV index with the news-reported index and found it was very accurate! It's a digital sensor that works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
  NEO-M8N GPS Module: GY-GPSV3-NEO NEO-M8N GPS Module Module based on U-blox NEO-M8N GPS engine, incorporating regulator for 3.3-5V DC input, MS621FE-compatible rechargeable battery for backup and EEPROM for storing configuration settings. Links: NEO-M8 series Product Summary NEO-M8 Datasheet
  APC220 with antenna: Radio transceiver module for Arduino operating in the 418-455MHz band.
